// Logisim project ngol.circ as structural Verilog: 6 circuits, main circuit cpu
module breadboard (
);

  wire cpu_1_clkp;
  wire [3:0] cpu_1_da_in_en_se, cpu_1_ram_sm1_sm_sr_er;
  wire [7:0] cpu_1_bus_out, cpu_1_out_2, cpu_1_out_3, cpu_1_out_4, cpu_1_out_5, cpu_1_out_7, cpu_1_out_8,
       cpu_1_out_9, cpu_1_out_10, hexadpt_1_hexo, ram_1_data, register_1_q, register_2_q;

  // Probe on cpu_1_out_3
  // Probe on cpu_1_out_2
  // Probe on cpu_1_clkp
  // Probe on cpu_1_out_7
  // Probe on cpu_1_out_5
  // Probe on cpu_1_out_4
  // Probe on cpu_1_out_8
  // Probe on cpu_1_out_10
  // Probe on cpu_1_out_9
  cpu cpu_1 (
    .da_in_en_se(cpu_1_da_in_en_se), .BUS_OUT(cpu_1_bus_out), .RAM_sm1_sm_sr_er(cpu_1_ram_sm1_sm_sr_er),
    .clkp(cpu_1_clkp), .out_7(cpu_1_out_7), .out_8(cpu_1_out_8), .out_9(cpu_1_out_9), .out_10(cpu_1_out_10),
    .out_2(cpu_1_out_2), .out_3(cpu_1_out_3), .out_4(cpu_1_out_4), .out_5(cpu_1_out_5), .BUSin(ram_1_data));
  hexadpt hexadpt_1 (.bus(cpu_1_bus_out), .hexo(hexadpt_1_hexo), .iobus_d_i_e_s(cpu_1_da_in_en_se));
  Register register_1 (.D(cpu_1_bus_out), .Q(register_1_q), .clk(cpu_1_ram_sm1_sm_sr_er[2]));  // open: en, clr
  Register register_2 (.D(cpu_1_bus_out), .Q(register_2_q), .clk(cpu_1_ram_sm1_sm_sr_er[3]));  // open: en, clr
  Hex_Digit_Display hex_digit_display_1 (.value(hexadpt_1_hexo[7:4]));  // open: dp
  RAM #(.addrWidth(16)) ram_1 (
    .addr({register_2_q, register_1_q}), .data(ram_1_data), .clk(cpu_1_ram_sm1_sm_sr_er[1]),
    .ld(cpu_1_ram_sm1_sm_sr_er[0]));  // open: sel, clr
  Hex_Digit_Display hex_digit_display_2 (.value(hexadpt_1_hexo[3:0]));  // open: dp

  // Notes on the sheet:
  //   Hex Display
  //   Adapter
endmodule

module cpu (
  input  [7:0] BUSin,
  output [7:0] out_2,
  output [7:0] out_3,
  output [7:0] out_4,
  output [7:0] out_5,
  output [3:0] RAM_sm1_sm_sr_er,
  output [7:0] out_7,
  output [7:0] out_8,
  output [7:0] out_9,
  output [7:0] out_10,
  output [7:0] BUS_OUT,
  output [3:0] da_in_en_se,
  output clkp
);

  wire and_3_out, and_4_out, and_5_out, bus1, c_in, control_1_e, control_1_s, counter_1_carry, ct, eacc, eb,
       ep, ep1, er, etmp, ld, ld1, not_1_out, not_2_out, not_3_out, not_4_out, not_5_out, not_6_out,
       pull_resistor_2_node, pull_resistor_4_node, rst, sacc, sflgs, sir, sp, sr, srsel, stmp;
  wire [1:0] demultiplexer_1_out0, demultiplexer_1_out1, demultiplexer_1_out2, demultiplexer_1_out3,
       demultiplexer_1_out4, demultiplexer_1_out5, demultiplexer_1_out6, demultiplexer_1_out7,
       pull_resistor_3_node;
  wire [2:0] control_1_aluop, controlled_buffer_9_out, ra, rb;
  wire [3:0] alu_1_z_e_g_c, control_1_fregprobe;
  wire [7:0] alu_1_o, counter_1_q, counter_2_q, register_9_q, register_10_q;
  wire [7:2] control_1_iro, control_1_out_9;
  wire [7:5] control_1_out_11;

  // Probe on control_1_e
  // Probe on control_1_s
  // Probe on da_in_en_se[2]
  // Probe on da_in_en_se[3]
  // Probe on and_5_out
  and and_1 (da_in_en_se[1], control_1_e, and_3_out);
  and and_2 (da_in_en_se[0], control_1_s, and_4_out);
  and and_3 (and_3_out, not_1_out, and_5_out);
  not not_1 (not_1_out, da_in_en_se[2]);
  assign pull_resistor_3_node[1] = and_5_out ? pull_resistor_2_node : 1'bz;  // Controlled_Buffer controlled_buffer_1
  Pull_Resistor pull_resistor_1 (.node(pull_resistor_3_node[1]));
  Pull_Resistor pull_resistor_2 (.node(pull_resistor_2_node));
  assign pull_resistor_2_node = and_3_out ? sr : 1'bz;  // Controlled_Buffer controlled_buffer_2
  and and_4 (and_4_out, da_in_en_se[2], and_5_out);
  Pull_Resistor pull_resistor_3 (.node(pull_resistor_3_node[0]));
  assign pull_resistor_3_node[0] = and_5_out ? pull_resistor_4_node : 1'bz;  // Controlled_Buffer controlled_buffer_3
  assign pull_resistor_3_node[1] = not_2_out ? sr : 1'bz;  // Controlled_Buffer controlled_buffer_4
  assign pull_resistor_3_node[0] = not_3_out ? er : 1'bz;  // Controlled_Buffer controlled_buffer_5
  not not_2 (not_2_out, and_5_out);
  not not_3 (not_3_out, and_5_out);
  not not_4 (not_4_out, control_1_iro[5]);
  and and_5 (and_5_out, control_1_iro[4], not_4_out, control_1_iro[6], not_5_out);
  not not_5 (not_5_out, control_1_iro[7]);
  Pull_Resistor pull_resistor_4 (.node(pull_resistor_4_node));
  assign pull_resistor_4_node = and_4_out ? er : 1'bz;  // Controlled_Buffer controlled_buffer_6
  // Probe on {control_1_iro, da_in_en_se[3:2]}
  // Probe on nothing
  Demultiplexer #(.select(3), .width(2), .disabled(0), .enable("false")) demultiplexer_1 (
    .out0(demultiplexer_1_out0), .out1(demultiplexer_1_out1), .out2(demultiplexer_1_out2),
    .out3(demultiplexer_1_out3), .out4(demultiplexer_1_out4), .out5(demultiplexer_1_out5),
    .out6(demultiplexer_1_out6), .out7(demultiplexer_1_out7), .in(pull_resistor_3_node),
    .sel(controlled_buffer_9_out));
  Clock clock_1 (.out(clkp));
  assign BUSin = demultiplexer_1_out0[0] ? out_2 : 8'bz;  // Controlled_Buffer controlled_buffer_7
  Register register_1 (.D(BUSin), .Q(out_3), .clk(demultiplexer_1_out1[1]));  // open: en, clr
  Register register_2 (.D(BUSin), .Q(out_2), .clk(demultiplexer_1_out0[1]));  // open: en, clr
  assign BUSin = demultiplexer_1_out4[0] ? out_7 : 8'bz;  // Controlled_Buffer controlled_buffer_8
  Register register_3 (.D(BUSin), .Q(out_7), .clk(demultiplexer_1_out4[1]));  // open: en, clr
  Register register_4 (.D(BUSin), .Q(out_8), .clk(demultiplexer_1_out5[1]));  // open: en, clr
  assign controlled_buffer_9_out = eb ? rb : 3'bz;  // Controlled_Buffer controlled_buffer_9
  assign controlled_buffer_9_out = not_6_out ? ra : 3'bz;  // Controlled_Buffer controlled_buffer_10
  not not_6 (not_6_out, eb);
  // Probe on ra
  Register register_5 (.D(BUSin), .Q(out_4), .clk(demultiplexer_1_out2[1]));  // open: en, clr
  assign BUSin = demultiplexer_1_out2[0] ? out_4 : 8'bz;  // Controlled_Buffer controlled_buffer_11
  assign BUSin = demultiplexer_1_out1[0] ? out_3 : 8'bz;  // Controlled_Buffer controlled_buffer_12
  assign BUSin = demultiplexer_1_out5[0] ? out_8 : 8'bz;  // Controlled_Buffer controlled_buffer_13
  assign BUSin = demultiplexer_1_out6[0] ? out_9 : 8'bz;  // Controlled_Buffer controlled_buffer_14
  Register register_6 (.D(BUSin), .Q(out_9), .clk(demultiplexer_1_out6[1]));  // open: en, clr
  // Probe on rb
  control control_1 (
    .in_6(alu_1_z_e_g_c), .busI(BUSin), .RA(ra), .RB(rb),
    .out_9({control_1_out_9, RAM_sm1_sm_sr_er[3], RAM_sm1_sm_sr_er[1]}),
    .out_10({RAM_sm1_sm_sr_er[2], sp, sr, stmp, sacc, sir, srsel, sflgs}),
    .out_11({control_1_out_11, ld1, ep1, rst, eb, er}),
    .out_12({ld, ct, ep, RAM_sm1_sm_sr_er[0], bus1, etmp, c_in, eacc}), .IIR(sir), .IRSel(srsel),
    .sflgs(sflgs), .aluop(control_1_aluop), .rst(rst), .fregprobe(control_1_fregprobe), .s(control_1_s),
    .e(control_1_e), .iro({control_1_iro, da_in_en_se[3:2]}));
  // Probe on control_1_fregprobe
  // Probe on BUSin
  Register register_7 (.D(BUSin), .Q(out_5), .clk(demultiplexer_1_out3[1]));  // open: en, clr
  assign BUSin = demultiplexer_1_out3[0] ? out_5 : 8'bz;  // Controlled_Buffer controlled_buffer_15
  Register register_8 (.D(BUSin), .Q(out_10), .clk(demultiplexer_1_out7[1]));  // open: en, clr
  assign BUSin = demultiplexer_1_out7[0] ? out_10 : 8'bz;  // Controlled_Buffer controlled_buffer_16
  // Probe on BUSin
  // Probe on control_1_aluop
  // Probe on alu_1_z_e_g_c
  Counter counter_1 (
    .load(ld), .D(BUSin), .count(ct), .Q(counter_1_q), .carry(counter_1_carry), .clk(sp));  // open: clr
  assign BUSin = etmp ? register_9_q : 8'bz;  // Controlled_Buffer controlled_buffer_17
  Register register_9 (.D(BUSin), .Q(register_9_q), .clk(stmp));  // open: en, clr
  // Probe on alu_1_o
  Counter counter_2 (.load(ld1), .D(BUSin), .count(counter_1_carry), .Q(counter_2_q), .clk(sp));  // open: carry, clr
  assign BUSin = ep1 ? counter_2_q : 8'bz;  // Controlled_Buffer controlled_buffer_18
  assign BUSin = ep ? counter_1_q : 8'bz;  // Controlled_Buffer controlled_buffer_19
  alu alu_1 (
    .A(BUSin), .B(register_9_q), .Cin(c_in), .z_e_g_c(alu_1_z_e_g_c), .O(alu_1_o), .OP(control_1_aluop),
    .bus1(bus1));
  Register register_10 (.D(alu_1_o), .Q(register_10_q), .clk(sacc));  // open: en, clr
  assign BUSin = eacc ? register_10_q : 8'bz;  // Controlled_Buffer controlled_buffer_20

  assign BUS_OUT = BUSin;

  // Other names for the same wires on the sheet: eram = RAM_sm1_sm_sr_er[0]; sram = RAM_sm1_sm_sr_er[1];
  //   smar = RAM_sm1_sm_sr_er[2]; smar1 = RAM_sm1_sm_sr_er[3]
endmodule

module alu (
  input  [7:0] B,
  input  bus1,
  input  [7:0] A,
  input  [2:0] OP,
  input  Cin,
  output [7:0] O,
  output [3:0] z_e_g_c
);

  wire adder_1_cout, and_3_out, and_4_out, not_2_out, not_3_out, not_4_out, not_5_out, not_6_out, not_7_out,
       not_8_out, not_9_out, not_10_out, not_11_out, not_12_out, not_13_out, not_14_out, subtractor_1_bout;
  wire [7:0] adder_1_out, and_1_out, multiplexer_1_out, not_1_out, shifter_1_out, shifter_2_out,
       subtractor_1_out, xor_1_out;

  Multiplexer #(.width(8), .disabled(0), .enable("false")) multiplexer_1 (
    .in0(B), .in1(8'h1), .out(multiplexer_1_out), .sel(bus1));
  Pull_Resistor pull_resistor_1 (.node(multiplexer_1_out));
  Pull_Resistor pull_resistor_2 (.node(A));
  Adder adder_1 (.a(A), .b(multiplexer_1_out), .out(adder_1_out), .cin(Cin), .cout(adder_1_cout));
  Subtractor subtractor_1 (.a(A), .b(multiplexer_1_out), .out(subtractor_1_out), .bin(Cin), .bout(subtractor_1_bout));
  Shifter shifter_1 (.in(A), .\dist (multiplexer_1_out[2:0]), .out(shifter_1_out));
  Shifter #(.shift("lr")) shifter_2 (.in(A), .\dist (multiplexer_1_out[2:0]), .out(shifter_2_out));
  assign and_1_out = A & multiplexer_1_out;  // AND_Gate and_1, 8 bits wide
  assign not_1_out = ~A;  // NOT_Gate not_1, 8 bits wide
  assign xor_1_out = A ^ multiplexer_1_out;  // XOR_Gate xor_1, 8 bits wide
  Comparator comparator_1 (.a(A), .b(multiplexer_1_out), .gt(z_e_g_c[1]), .eq(z_e_g_c[2]));  // open: lt
  not not_2 (not_2_out, A[0]);
  not not_3 (not_3_out, A[1]);
  not not_4 (not_4_out, A[2]);
  not not_5 (not_5_out, A[3]);
  not not_6 (not_6_out, A[4]);
  not not_7 (not_7_out, A[5]);
  not not_8 (not_8_out, A[6]);
  not not_9 (not_9_out, A[7]);
  assign z_e_g_c[0] = and_3_out ? subtractor_1_bout : 1'bz;  // Controlled_Buffer controlled_buffer_1
  and and_2 (z_e_g_c[3], not_2_out, not_3_out, not_4_out, not_5_out, not_6_out, not_7_out, not_8_out, not_9_out);
  Multiplexer #(.select(3), .width(8), .disabled(0), .enable("false")) multiplexer_2 (
    .in0(adder_1_out), .in1(subtractor_1_out), .in2(shifter_1_out), .in3(shifter_2_out), .in4(and_1_out),
    .in5(not_1_out), .in6(xor_1_out), .out(O), .sel(OP));  // open: in7
  not not_10 (not_10_out, OP[0]);
  not not_11 (not_11_out, OP[1]);
  not not_12 (not_12_out, OP[2]);
  not not_13 (not_13_out, OP[2]);
  not not_14 (not_14_out, OP[1]);
  and and_3 (and_3_out, not_13_out, not_14_out, OP[0]);
  and and_4 (and_4_out, not_12_out, not_11_out, not_10_out);
  Pull_Resistor pull_resistor_3 (.node(z_e_g_c[0]));
  assign z_e_g_c[0] = and_4_out ? adder_1_cout : 1'bz;  // Controlled_Buffer controlled_buffer_2
  Pull_Resistor pull_resistor_4 (.node(O));
endmodule

module control (
  input  [7:0] busI,
  input  IRSel,
  input  IIR,
  input  rst,
  input  sflgs,
  input  [3:0] in_6,
  output [2:0] RA,
  output [2:0] RB,
  output [7:0] out_9,
  output [7:0] out_10,
  output [7:0] out_11,
  output [7:0] out_12,
  output [7:0] iro,
  output e,
  output s,
  output [3:0] fregprobe,
  output [2:0] aluop
);

  wire and_1_out, and_2_out, and_3_out, and_4_out, and_5_out, and_6_out, clock_1_out, decoder_1_out1,
       decoder_1_out3, not_1_out, not_2_out, or_2_out;
  wire [1:0] I_OCYCLE_q;
  wire [2:0] RSel_q_2, STEP_q;
  wire [7:0] rom_1_data_2, rom_1_data_3;
  wire [7:3] RSel_q;
  wire [7:7] or_3_out;
  wire [15:0] rom_1_data;

  Counter #(.width(2), .max('h3)) I_OCYCLE (.Q(I_OCYCLE_q), .clk(clock_1_out));  // open: load, D, count, carry, clr
  Clock clock_1 (.out(clock_1_out));
  or or_1 (e, decoder_1_out1, s, decoder_1_out3);
  Decoder #(.select(2), .disabled(0), .enable("false")) decoder_1 (
    .out1(decoder_1_out1), .out2(s), .out3(decoder_1_out3), .sel(I_OCYCLE_q));  // open: out0
  Counter #(.width(3), .max('h7), .trigger("falling")) STEP (
    .Q(STEP_q), .clk(decoder_1_out3), .clr(or_2_out));  // open: load, D, count, carry
  or or_2 (or_2_out, rst, and_1_out);
  assign RA = iro[7] ? RSel_q_2 : 3'bz;  // Controlled_Buffer controlled_buffer_1
  Register RSel (.D(busI), .Q({RSel_q[7], RSel_q_2, RSel_q[3], RB}), .clk(IRSel));  // open: en, clr
  Register IR (.D(busI), .Q({iro[7:3], aluop}), .clk(IIR));  // open: en, clr
  not not_1 (not_1_out, STEP_q[0]);
  and and_1 (and_1_out, not_1_out, STEP_q[1], STEP_q[2], aluop[0], aluop[1], aluop[2]);
  assign RA = not_2_out ? aluop : 3'bz;  // Controlled_Buffer controlled_buffer_2
  not not_2 (not_2_out, iro[7]);
  assign out_9 = s ? rom_1_data_3 : 8'bz;  // Controlled_Buffer controlled_buffer_3
  Pull_Resistor pull_resistor_1 (.node(out_9));
  Pull_Resistor pull_resistor_2 (.node(out_10));
  assign out_10 = s ? rom_1_data_2 : 8'bz;  // Controlled_Buffer controlled_buffer_4
  or or_3 (or_3_out[7], and_5_out, and_4_out, and_6_out, and_3_out, and_2_out);
  and and_2 (and_2_out, fregprobe[3], iro[3]);
  and and_3 (and_3_out, fregprobe[2], aluop[2]);
  and and_4 (and_4_out, fregprobe[1], aluop[1]);
  and and_5 (and_5_out, fregprobe[0], aluop[0]);
  assign out_11 = e ? rom_1_data[15:8] : 8'bz;  // Controlled_Buffer controlled_buffer_5
  Pull_Resistor pull_resistor_3 (.node(out_11));
  Register #(.width(4)) register_1 (.D(in_6), .Q(fregprobe), .clk(sflgs));  // open: en, clr
  ROM #(.dataWidth(32)) rom_1 (
    .addr({or_3_out[7], iro[7:4], STEP_q}), .data({rom_1_data_3, rom_1_data_2, rom_1_data}));  // open: sel
  and and_6 (and_6_out, aluop[0], aluop[1], aluop[2], iro[3], fregprobe[0], fregprobe[1], fregprobe[2], fregprobe[3]);
  Pull_Resistor pull_resistor_4 (.node(out_12));
  assign out_12 = e ? rom_1_data[7:0] : 8'bz;  // Controlled_Buffer controlled_buffer_6
  // Probe on s
  // Probe on e

  assign iro[2:0] = aluop;

  // Notes on the sheet:
  //   contents of rom_1 (hex, n*v repeats v):
  //   800020 440050 400 5*0 800020 440050 800020 600050 400 0 0 0 800020 440050 800020 c00050 1000100 400
  //   0 0 800020 440050 800020 c00050 200010 400 0 0 800020 440050 400040 400 4*0 800020 440050 800020
  //   420050 200100 400 0 0 800020 440050 80108 200001 400 0 0 0 800020 440050 400 5*0 800020 440050
  //   800020 420050 100300 90100 200001 400 800020 440050 400 5*0 800020 440050 400 5*0 800020 440050 400
  //   5*0 800020 440050 400 5*0 800020 440050 400 5*0 800020 440050 400 5*0 800020 440050 400 5*0 800020
  //   440050 400 5*0 800020 440050 800020 600050 400 0 0 0 800020 440050 800020 c00050 1000100 400 0 0
  //   800020 440050 800020 c00050 200010 400 0 0 800020 440050 800020 400090 400 0 0 0 800020 440050
  //   800020 420050 200100 400 0 0 800020 440050 80108 200001 400 0 0 0 800020 440050 400 5*0 800020
  //   440050 800020 420050 100300 90100 200001 400 800020 440050 6*0 800020 440050 6*0 800020 440050 6*0
  //   800020 440050 6*0 800020 440050 6*0 800020 440050 6*0 800020 440050
endmodule

module hexadpt (
  input  [3:0] iobus_d_i_e_s,
  input  [7:0] bus,
  output [7:0] hexo
);

  wire and_1_out, and_2_out, and_3_out, and_4_out, not_1_out, not_2_out, not_3_out, not_4_out, not_5_out,
       not_6_out, t_ff_1_q;

  not not_1 (not_1_out, bus[0]);
  and and_1 (and_1_out, not_1_out, bus[1], bus[2], bus[3], not_2_out, not_3_out, not_4_out, not_5_out);
  not not_2 (not_2_out, bus[4]);
  not not_3 (not_3_out, bus[5]);
  not not_4 (not_4_out, bus[6]);
  not not_5 (not_5_out, bus[7]);
  and and_2 (and_2_out, iobus_d_i_e_s[0], iobus_d_i_e_s[2], not_6_out);
  not not_6 (not_6_out, iobus_d_i_e_s[3]);
  and and_3 (and_3_out, iobus_d_i_e_s[2], iobus_d_i_e_s[3], iobus_d_i_e_s[0]);
  T_Flip_Flop t_ff_1 (.clk(and_3_out), .T(and_1_out), .Q(t_ff_1_q));  // open: Qn, preset, reset, en
  Register register_1 (.D(bus), .Q(hexo), .clk(and_4_out));  // open: en, clr
  and and_4 (and_4_out, and_2_out, t_ff_1_q);
endmodule

module testbed (
  input  sram,
  input  eram,
  input  smar,
  input  smar1,
  input  smar_2,
  input  ld,
  input  ct,
  input  ld1,
  input  smar1_2,
  input  clk,
  input  epc,
  input  [7:0] in_12,
  input  in_13,
  input  in_14,
  input  in_15,
  input  epc1
);

  wire and_1_out, and_2_out, counter_1_carry, not_1_out, or_1_out, t_ff_1_q;
  wire [7:0] controlled_buffer_1_out, controlled_buffer_3_out, counter_1_q, counter_2_q, ram_1_data,
       register_1_q, register_2_q, register_3_q, register_4_q, undriven;

  Counter counter_1 (
    .load(ld), .D(undriven), .count(ct), .Q(counter_1_q), .carry(counter_1_carry), .clk(clk));  // open: clr
  T_Flip_Flop t_ff_1 (.clk(clk), .T(counter_1_carry), .Q(t_ff_1_q), .reset(and_2_out));  // open: Qn, preset, en
  Counter counter_2 (
    .load(ld1), .D(undriven), .count(counter_1_carry), .Q(counter_2_q), .clk(clk));  // open: carry, clr
  // Probe on ram_1_data
  assign controlled_buffer_1_out = epc ? counter_1_q : 8'bz;  // Controlled_Buffer controlled_buffer_1
  assign controlled_buffer_1_out = epc1 ? counter_2_q : 8'bz;  // Controlled_Buffer controlled_buffer_2
  assign controlled_buffer_3_out = not_1_out ? controlled_buffer_1_out : 8'bz;  // Controlled_Buffer controlled_buffer_3
  not not_1 (not_1_out, and_1_out);
  assign controlled_buffer_3_out = and_1_out ? counter_2_q : 8'bz;  // Controlled_Buffer controlled_buffer_4
  and and_1 (and_1_out, t_ff_1_q, epc);
  or or_1 (or_1_out, and_2_out, smar1_2);
  and and_2 (and_2_out, t_ff_1_q, smar_2);
  Register register_1 (.D(ram_1_data), .Q(register_1_q), .clk(smar));  // open: en, clr
  Register register_2 (.D(ram_1_data), .Q(register_2_q), .clk(smar1));  // open: en, clr
  Register register_3 (.D(controlled_buffer_1_out), .Q(register_3_q), .clk(smar_2));  // open: en, clr
  Register register_4 (.D(controlled_buffer_3_out), .Q(register_4_q), .clk(or_1_out));  // open: en, clr
  RAM #(.addrWidth(16)) ram_1 (
    .addr({register_2_q, register_1_q}), .data(ram_1_data), .clk(sram), .ld(eram));  // open: sel, clr
  RAM #(.addrWidth(16)) ram_2 (.addr({register_4_q, register_3_q}));  // open: data, sel, clk, ld, clr
endmodule
